// Logisim project decoder-2bit.circ as structural Verilog: 1 circuit, main circuit main
module main (
  input  x,
  input  y,
  output d0,
  output d1,
  output d2,
  output d3
);

  wire not_1_out, not_2_out;

  not not_1 (not_1_out, x);
  not not_2 (not_2_out, y);
  and and_1 (d0, not_1_out, not_2_out);
  and and_2 (d1, x, not_2_out);
  and and_3 (d2, y, not_1_out);
  and and_4 (d3, y, x);

  // Notes on the sheet:
  //   x
  //   y
  //   0
  //   0
  //   1
  //   0
  //   1
  //   0
  //   1
  //   1
  //   d0
  //   d1
  //   0
  //   1
  //   1
  //   0
  //   0
  //   0
  //   0
  //   0
  //   d - mintermos
  //   d2
  //   d3
  //   0
  //   0
  //   0
  //   0
  //   0
  //   1
  //   0
  //   1
endmodule
