// Logisim project demux-2bit.circ as structural Verilog: 1 circuit, main circuit main
module main (
  input  x,
  input  s,
  output f0,
  output f1
);

  wire not_1_out;

  not not_1 (not_1_out, s);
  and and_1 (f0, x, not_1_out);
  and and_2 (f1, x, s);
endmodule
