// Logisim project demux-4bit.circ as structural Verilog: 1 circuit, main circuit main
module main (
  input  x,
  input  s0,
  input  s1,
  output f0,
  output f1,
  output f2,
  output f3
);

  wire not_1_out, not_2_out, not_3_out, not_4_out;

  not not_1 (not_1_out, s0);
  not not_2 (not_2_out, s1);
  not not_3 (not_3_out, s0);
  not not_4 (not_4_out, s1);
  and and_1 (f0, x, not_1_out, not_2_out);
  and and_2 (f1, x, not_3_out, s1);
  and and_3 (f2, x, s0, not_4_out);
  and and_4 (f3, x, s0, s1);
endmodule
