// Logisim project encoder-2bit.circ as structural Verilog: 1 circuit, main circuit main
module main (
  input  x1,
  input  x3,
  input  x2,
  output f0,
  output f1
);

  wire not_1_out, not_2_out, not_3_out, not_4_out;

  not not_1 (not_1_out, x1);
  not not_2 (not_2_out, x3);
  not not_3 (not_3_out, x3);
  not not_4 (not_4_out, x2);
  or or_1 (f0, not_1_out, not_2_out);
  or or_2 (f1, not_3_out, not_4_out);
endmodule
