// Logisim project encoder-3bit.circ as structural Verilog: 1 circuit, main circuit main
module main (
  input  x1,
  input  x2,
  input  x3,
  input  x4,
  input  x5,
  input  x6,
  input  x7,
  output f0,
  output f1,
  output f2
);

  wire not_1_out, not_2_out, not_3_out, not_4_out, not_5_out, not_6_out, not_7_out, not_8_out, not_9_out,
       not_10_out, not_11_out, not_12_out;

  not not_1 (not_1_out, x1);
  not not_2 (not_2_out, x3);
  not not_3 (not_3_out, x5);
  not not_4 (not_4_out, x7);
  not not_5 (not_5_out, x2);
  not not_6 (not_6_out, x3);
  not not_7 (not_7_out, x6);
  not not_8 (not_8_out, x7);
  not not_9 (not_9_out, x4);
  not not_10 (not_10_out, x5);
  not not_11 (not_11_out, x6);
  not not_12 (not_12_out, x7);
  or or_1 (f0, not_1_out, not_2_out, not_3_out, not_4_out);
  or or_2 (f1, not_5_out, not_6_out, not_7_out, not_8_out);
  or or_3 (f2, not_9_out, not_10_out, not_11_out, not_12_out);
endmodule
