// Logisim project fulladder.circ as structural Verilog: 1 circuit, main circuit main
module main (
  input  A,
  input  Vem_um,
  input  B,
  output S,
  output Vai_um
);

  wire and_1_out, and_2_out, xor_1_out;

  xor xor_1 (xor_1_out, A, B);
  and and_1 (and_1_out, A, B);
  and and_2 (and_2_out, xor_1_out, Vem_um);
  xor xor_2 (S, xor_1_out, Vem_um);
  or or_1 (Vai_um, and_2_out, and_1_out);
endmodule
