// Logisim project halfadder.circ as structural Verilog: 1 circuit, main circuit main
module main (
  input  A,
  input  B,
  output Soma,
  output Vai_um
);

  xor xor_1 (Soma, A, B);
  and and_1 (Vai_um, A, B);
endmodule
