// Logisim project latch-nand.circ as structural Verilog: 1 circuit, main circuit main
module main (
  input  SET,
  input  CLEAR,
  output Q,
  output NOT_Q
);

  nand nand_1 (Q, SET, NOT_Q);
  nand nand_2 (NOT_Q, Q, CLEAR);

  // Notes on the sheet:
  //   SET
  //   1
  //   0
  //   1
  //   0
  //   CLEAR
  //   1
  //   1
  //   0
  //   0
  //   SAIDA
  //   Nao muda
  //   Q=1
  //   Q=0
  //   Inválida
  //   A entrada CLEAR também pode ser chamada de RESET
  //   a. Repouso - SET=CLEAR=1
  //   b. SET=0, força Q=1
  //   c. CLEAR=0, força Q=0
  //   LATCH NAND
endmodule
