// Logisim project latch-nor.circ as structural Verilog: 1 circuit, main circuit main
module main (
  input  SET,
  input  CLEAR,
  output NOT_Q,
  output Q
);

  wire undriven, undriven_2;

  nor nor_1 (NOT_Q, SET, undriven_2);
  nor nor_2 (Q, undriven, CLEAR);

  // Notes on the sheet:
  //   SET
  //   0
  //   1
  //   0
  //   1
  //   CLEAR
  //   0
  //   0
  //   1
  //   1
  //   SAIDA
  //   Nao muda
  //   Q=1
  //   Q=0
  //   Inválida
  //   A entrada CLEAR também pode ser chamada de RESET
  //   a. Repouso - SET=CLEAR=0
  //   b. SET=1, força Q=1
  //   c. CLEAR=1, força Q=0
  //   LATCH NOR
endmodule
