// Logisim project somadorParcial.circ as structural Verilog: 1 circuit, main circuit main
module main (
  input  A,
  input  B,
  output SOMA,
  output VAI_UM
);

  and and_1 (VAI_UM, A, B);
  xor xor_1 (SOMA, A, B);

  // Notes on the sheet:
  //   XOR
  //   B
  //   A
  //   0
  //   0
  //   1
  //   0
  //   1
  //   0
  //   1
  //   1
  //   SOMA
  //   0
  //   1
  //   1
  //   0
  //   VAI_UM
  //   0
  //   0
  //   0
  //   1
endmodule
